// Logisim project risc_v_new.circ as structural Verilog: 1 circuit, main circuit main
module main (
);

  wire and_1_out, and_3_out, button_1_out, button_2_out, clock_1_out, comparator_1_eq, comparator_1_lt,
       comparator_2_eq, comparator_2_lt, comparator_3_lt, comparator_4_lt, decoder_1_out1, decoder_1_out2,
       decoder_1_out3, decoder_1_out4, decoder_1_out5, decoder_1_out6, decoder_1_out7, decoder_1_out8,
       decoder_1_out9, decoder_1_out10, decoder_1_out11, decoder_1_out12, decoder_1_out13, decoder_1_out14,
       decoder_1_out15, decoder_1_out16, decoder_1_out17, decoder_1_out18, decoder_1_out19, decoder_1_out20,
       decoder_1_out21, decoder_1_out22, decoder_1_out23, decoder_1_out24, decoder_1_out25, decoder_1_out26,
       decoder_1_out27, decoder_1_out28, decoder_1_out29, decoder_1_out30, decoder_1_out31, decoder_2_out1,
       decoder_2_out2, decoder_2_out3, decoder_3_out0, decoder_3_out2, decoder_4_out0, decoder_4_out1,
       decoder_4_out3, decoder_5_out2, decoder_5_out3, decoder_5_out4, decoder_5_out5, dipswitch_1_sw1,
       keyboard_1_avail, multiplexer_10_out, multiplexer_11_out, multiplexer_12_out, multiplexer_13_out,
       multiplexer_20_out, multiplexer_21_out, nor_1_out, not_1_out, not_2_out, not_3_out, not_4_out,
       not_5_out, not_6_out, or_2_out, or_3_out;
  wire [1:0] CIR_q_4, counter_1_q;
  wire [2:0] multiplexer_22_out, ROM_3_data;
  wire [3:0] bit_extender_4_out, bit_extender_5_out, bit_extender_6_out, bit_extender_7_out,
       bit_extender_8_out, bit_extender_9_out, bit_extender_10_out, bit_extender_11_out, bit_extender_12_out,
       bit_extender_13_out, x18_s2_q, x18_s2_q_2, x18_s2_q_3, x18_s2_q_4, x18_s2_q_5, x18_s2_q_6, x18_s2_q_7,
       x18_s2_q_8;
  wire [3:3] CIR_q_5;
  wire [4:0] CIR_q_2, CIR_q_3, CIR_q_6, multiplexer_2_out, multiplexer_14_out;
  wire [4:3] ROM_2_data_2;
  wire [5:0] multiplexer_8_out;
  wire [6:0] bit_extender_1_out, keyboard_1_data, ROM_2_data;
  wire [7:0] bit_extender_19_out, ROM_1_data;
  wire [15:0] bit_extender_16_out;
  wire [25:0] multiplexer_8_out_2;
  wire [31:0] adder_1_out, adder_2_out, and_2_out, bit_extender_2_out, bit_extender_3_out,
       bit_extender_14_out, bit_extender_15_out, bit_extender_17_out, bit_extender_18_out,
       bit_extender_20_out, bit_extender_21_out, bit_extender_22_out, bit_extender_23_out,
       bit_extender_24_out, bit_extender_25_out, CIR_q, divider_1_out, divider_1_rem, divider_2_out,
       divider_2_rem, divider_3_out, divider_3_rem, divider_4_out, divider_4_rem, divider_5_out,
       divider_5_rem, divider_6_out, divider_6_rem, divider_7_out, divider_7_rem, divider_8_out,
       divider_8_rem, divider_9_out, divider_9_rem, divider_10_rem, multiplexer_1_out, multiplexer_3_out,
       multiplexer_4_out, multiplexer_5_out, multiplexer_6_out, multiplexer_7_out, multiplexer_9_out,
       multiplexer_15_out, multiplexer_16_out, multiplexer_17_out, multiplexer_18_out, multiplexer_19_out,
       multiplexer_23_out, or_1_out, PC4buf_q, PC_q, PCbuf_q, RAM_1_dout, shifter_1_out, shifter_2_out,
       shifter_3_out, shifter_4_out, shifter_5_out, subtractor_1_out, x0_zero_q, x1_ra_q, x2_sp_q, x3_gp_q,
       x4_tp_q, x5_t0_q, x6_t1_q, x7_t2_q, x8_s0_fp_q, x9_s1_q, x10_a0_q, x11_a1_q, x12_a2_q, x13_a3_q,
       x14_a4_q, x15_a5_q, x16_a6_q, x17_a7_q, x19_s3_q, x20_s4_q, x21_s5_q, x22_s6_q, x23_s7_q, x24_s8_q,
       x25_s9_q, x26_s10_q, x27_s11_q, x28_t3_q, x29_t4_q, x30_t5_q, x31_t6_q, xor_1_out;

  Decoder #(.enable("false"), .select(5)) decoder_1 (
    .out1(decoder_1_out1), .out2(decoder_1_out2), .out3(decoder_1_out3), .out4(decoder_1_out4),
    .out5(decoder_1_out5), .out6(decoder_1_out6), .out7(decoder_1_out7), .out8(decoder_1_out8),
    .out9(decoder_1_out9), .out10(decoder_1_out10), .out11(decoder_1_out11), .out12(decoder_1_out12),
    .out13(decoder_1_out13), .out14(decoder_1_out14), .out15(decoder_1_out15), .out16(decoder_1_out16),
    .out17(decoder_1_out17), .out18(decoder_1_out18), .out19(decoder_1_out19), .out20(decoder_1_out20),
    .out21(decoder_1_out21), .out22(decoder_1_out22), .out23(decoder_1_out23), .out24(decoder_1_out24),
    .out25(decoder_1_out25), .out26(decoder_1_out26), .out27(decoder_1_out27), .out28(decoder_1_out28),
    .out29(decoder_1_out29), .out30(decoder_1_out30), .out31(decoder_1_out31), .sel(multiplexer_14_out));  // open: out0
  Register #(.width(32)) x0_zero (
    .D(multiplexer_4_out), .en(1'b0), .clk(decoder_4_out3), .Q(x0_zero_q), .clr(button_1_out));
  Register #(.width(32)) x1_ra (
    .D(multiplexer_4_out), .en(decoder_1_out1), .clk(decoder_4_out3), .Q(x1_ra_q), .clr(button_1_out));
  Register #(.width(32)) x2_sp (
    .D(multiplexer_4_out), .en(decoder_1_out2), .clk(decoder_4_out3), .Q(x2_sp_q), .clr(button_1_out));
  Register #(.width(32)) x3_gp (
    .D(multiplexer_4_out), .en(decoder_1_out3), .clk(decoder_4_out3), .Q(x3_gp_q), .clr(button_1_out));
  Register #(.width(32)) x4_tp (
    .D(multiplexer_4_out), .en(decoder_1_out4), .clk(decoder_4_out3), .Q(x4_tp_q), .clr(button_1_out));
  Register #(.width(32)) x5_t0 (
    .D(multiplexer_4_out), .en(decoder_1_out5), .clk(decoder_4_out3), .Q(x5_t0_q), .clr(button_1_out));
  Register #(.width(32)) x6_t1 (
    .D(multiplexer_4_out), .en(decoder_1_out6), .clk(decoder_4_out3), .Q(x6_t1_q), .clr(button_1_out));
  Register #(.width(32)) x7_t2 (
    .D(multiplexer_4_out), .en(decoder_1_out7), .clk(decoder_4_out3), .Q(x7_t2_q), .clr(button_1_out));
  Register #(.width(32)) x8_s0_fp (
    .D(multiplexer_4_out), .en(decoder_1_out8), .clk(decoder_4_out3), .Q(x8_s0_fp_q), .clr(button_1_out));
  Register #(.width(32)) x9_s1 (
    .D(multiplexer_4_out), .en(decoder_1_out9), .clk(decoder_4_out3), .Q(x9_s1_q), .clr(button_1_out));
  Register #(.width(32)) x10_a0 (
    .D(multiplexer_4_out), .en(decoder_1_out10), .clk(decoder_4_out3), .Q(x10_a0_q), .clr(button_1_out));
  Register #(.width(32)) x11_a1 (
    .D(multiplexer_4_out), .en(decoder_1_out11), .clk(decoder_4_out3), .Q(x11_a1_q), .clr(button_1_out));
  Register #(.width(32)) x12_a2 (
    .D(multiplexer_4_out), .en(decoder_1_out12), .clk(decoder_4_out3), .Q(x12_a2_q), .clr(button_1_out));
  Register #(.width(32)) x13_a3 (
    .D(multiplexer_4_out), .en(decoder_1_out13), .clk(decoder_4_out3), .Q(x13_a3_q), .clr(button_1_out));
  Register #(.width(32)) x14_a4 (
    .D(multiplexer_4_out), .en(decoder_1_out14), .clk(decoder_4_out3), .Q(x14_a4_q), .clr(button_1_out));
  Register #(.width(32)) x15_a5 (
    .D(multiplexer_4_out), .en(decoder_1_out15), .clk(decoder_4_out3), .Q(x15_a5_q), .clr(button_1_out));
  Register #(.width(32)) x16_a6 (
    .D(multiplexer_4_out), .en(decoder_1_out16), .clk(decoder_4_out3), .Q(x16_a6_q), .clr(button_1_out));
  Register #(.width(32)) x17_a7 (
    .D(multiplexer_4_out), .en(decoder_1_out17), .clk(decoder_4_out3), .Q(x17_a7_q), .clr(button_1_out));
  Register #(.width(32)) x18_s2 (
    .D(multiplexer_4_out), .en(decoder_1_out18), .clk(decoder_4_out3),
    .Q({x18_s2_q_8, x18_s2_q_7, x18_s2_q_6, x18_s2_q_5, x18_s2_q_4, x18_s2_q_3, x18_s2_q_2, x18_s2_q}),
    .clr(button_1_out));
  Register #(.width(32)) x19_s3 (
    .D(multiplexer_4_out), .en(decoder_1_out19), .clk(decoder_4_out3), .Q(x19_s3_q), .clr(button_1_out));
  Register #(.width(32)) x20_s4 (
    .D(multiplexer_4_out), .en(decoder_1_out20), .clk(decoder_4_out3), .Q(x20_s4_q), .clr(button_1_out));
  Register #(.width(32)) x21_s5 (
    .D(multiplexer_4_out), .en(decoder_1_out21), .clk(decoder_4_out3), .Q(x21_s5_q), .clr(button_1_out));
  Register #(.width(32)) x22_s6 (
    .D(multiplexer_4_out), .en(decoder_1_out22), .clk(decoder_4_out3), .Q(x22_s6_q), .clr(button_1_out));
  Register #(.width(32)) x23_s7 (
    .D(multiplexer_4_out), .en(decoder_1_out23), .clk(decoder_4_out3), .Q(x23_s7_q), .clr(button_1_out));
  Register #(.width(32)) x24_s8 (
    .D(multiplexer_4_out), .en(decoder_1_out24), .clk(decoder_4_out3), .Q(x24_s8_q), .clr(button_1_out));
  Register #(.width(32)) x25_s9 (
    .D(multiplexer_4_out), .en(decoder_1_out25), .clk(decoder_4_out3), .Q(x25_s9_q), .clr(button_1_out));
  Register #(.width(32)) x26_s10 (
    .D(multiplexer_4_out), .en(decoder_1_out26), .clk(decoder_4_out3), .Q(x26_s10_q), .clr(button_1_out));
  Register #(.width(32)) x27_s11 (
    .D(multiplexer_4_out), .en(decoder_1_out27), .clk(decoder_4_out3), .Q(x27_s11_q), .clr(button_1_out));
  Register #(.width(32)) x28_t3 (
    .D(multiplexer_4_out), .en(decoder_1_out28), .clk(decoder_4_out3), .Q(x28_t3_q), .clr(button_1_out));
  Register #(.width(32)) x29_t4 (
    .D(multiplexer_4_out), .en(decoder_1_out29), .clk(decoder_4_out3), .Q(x29_t4_q), .clr(button_1_out));
  Register #(.width(32)) x30_t5 (
    .D(multiplexer_4_out), .en(decoder_1_out30), .clk(decoder_4_out3), .Q(x30_t5_q), .clr(button_1_out));
  Register #(.width(32)) x31_t6 (
    .D(multiplexer_4_out), .en(decoder_1_out31), .clk(decoder_4_out3), .Q(x31_t6_q), .clr(button_1_out));
  Multiplexer #(.select(5), .width(32)) multiplexer_1 (
    .in0(x0_zero_q), .in1(x1_ra_q), .in2(x2_sp_q), .in3(x3_gp_q), .in4(x4_tp_q), .in5(x5_t0_q),
    .in6(x6_t1_q), .in7(x7_t2_q), .in8(x8_s0_fp_q), .in9(x9_s1_q), .in10(x10_a0_q), .in11(x11_a1_q),
    .in12(x12_a2_q), .in13(x13_a3_q), .in14(x14_a4_q), .in15(x15_a5_q), .in16(x16_a6_q), .in17(x17_a7_q),
    .in18({x18_s2_q_8, x18_s2_q_7, x18_s2_q_6, x18_s2_q_5, x18_s2_q_4, x18_s2_q_3, x18_s2_q_2, x18_s2_q}),
    .in19(x19_s3_q), .in20(x20_s4_q), .in21(x21_s5_q), .in22(x22_s6_q), .in23(x23_s7_q), .in24(x24_s8_q),
    .in25(x25_s9_q), .in26(x26_s10_q), .in27(x27_s11_q), .in28(x28_t3_q), .in29(x29_t4_q), .in30(x30_t5_q),
    .in31(x31_t6_q), .out(multiplexer_1_out), .sel(multiplexer_2_out));
  Multiplexer #(.width(5)) multiplexer_2 (.in0(CIR_q_6), .in1({5{1'b0}}), .out(multiplexer_2_out), .sel(or_3_out));
  Multiplexer #(.select(5), .width(32)) multiplexer_3 (
    .in0(x0_zero_q), .in1(x1_ra_q), .in2(x2_sp_q), .in3(x3_gp_q), .in4(x4_tp_q), .in5(x5_t0_q),
    .in6(x6_t1_q), .in7(x7_t2_q), .in8(x8_s0_fp_q), .in9(x9_s1_q), .in10(x10_a0_q), .in11(x11_a1_q),
    .in12(x12_a2_q), .in13(x13_a3_q), .in14(x14_a4_q), .in15(x15_a5_q), .in16(x16_a6_q), .in17(x17_a7_q),
    .in18({x18_s2_q_8, x18_s2_q_7, x18_s2_q_6, x18_s2_q_5, x18_s2_q_4, x18_s2_q_3, x18_s2_q_2, x18_s2_q}),
    .in19(x19_s3_q), .in20(x20_s4_q), .in21(x21_s5_q), .in22(x22_s6_q), .in23(x23_s7_q), .in24(x24_s8_q),
    .in25(x25_s9_q), .in26(x26_s10_q), .in27(x27_s11_q), .in28(x28_t3_q), .in29(x29_t4_q), .in30(x30_t5_q),
    .in31(x31_t6_q), .out(multiplexer_3_out), .sel(CIR_q_3));
  ROM #(.addrWidth(6), .dataWidth(3)) ROM_3 (.addr(multiplexer_8_out), .data(ROM_3_data));
  Bit_Extender #(.in_width(32), .out_width(7)) bit_extender_1 (.in(multiplexer_3_out), .out(bit_extender_1_out));
  Register #(.width(32)) PCbuf (.D(PC_q), .en(1'b1), .clk(decoder_4_out1), .Q(PCbuf_q), .clr(button_1_out));
  Register #(.width(32)) PC (.D(multiplexer_9_out), .en(1'b1), .clk(decoder_4_out3), .Q(PC_q), .clr(button_1_out));
  Multiplexer #(.select(2), .width(32)) multiplexer_4 (
    .in1(PC4buf_q), .in2(multiplexer_19_out), .in3(multiplexer_17_out), .out(multiplexer_4_out),
    .sel(ROM_1_data[4:3]));  // open: in0
  TTY tty_1 (.data(bit_extender_1_out), .clk(and_1_out), .we(decoder_2_out2), .clr(button_1_out));
  Keyboard keyboard_1 (
    .clk(and_1_out), .re(decoder_2_out3), .clr(button_1_out), .avail(keyboard_1_avail), .data(keyboard_1_data));
  assign bit_extender_2_out = {{31{1'b0}}, keyboard_1_avail};  // Bit_Extender bit_extender_2
  assign bit_extender_3_out = {{25{1'b0}}, keyboard_1_data};  // Bit_Extender bit_extender_3
  Multiplexer #(.width(32)) multiplexer_5 (
    .in0(bit_extender_2_out), .in1(bit_extender_3_out), .out(multiplexer_5_out), .sel(multiplexer_8_out_2[0]));
  and and_1 (and_1_out, decoder_4_out3, decoder_5_out2);
  Shifter #(.width(32)) shifter_1 (.in(multiplexer_3_out), .\dist ({ROM_2_data_2, 3'b000}), .out(shifter_1_out));
  Divider #(.width(32)) divider_1 (
    .a({x18_s2_q_8, x18_s2_q_7, x18_s2_q_6, x18_s2_q_5, x18_s2_q_4, x18_s2_q_3, x18_s2_q_2, x18_s2_q}),
    .b(32'ha), .out(divider_1_out), .rem(divider_1_rem));  // open: upper
  Divider #(.width(32)) divider_2 (
    .a(divider_1_out), .b(32'ha), .out(divider_2_out), .rem(divider_2_rem));  // open: upper
  Bit_Extender #(.in_width(32), .out_width(4)) bit_extender_4 (.in(divider_1_rem), .out(bit_extender_4_out));
  Multiplexer #(.width(32)) multiplexer_6 (
    .in0(multiplexer_1_out), .in1(PCbuf_q), .out(multiplexer_6_out), .sel(ROM_1_data[6]));
  Multiplexer #(.width(32)) multiplexer_7 (
    .in0(multiplexer_23_out), .in1(multiplexer_3_out), .out(multiplexer_7_out), .sel(ROM_1_data[7]));
  Adder #(.width(32)) adder_1 (.a(32'h4), .b(PC_q), .out(adder_1_out), .cin(1'b0));  // open: cout
  Register #(.width(32)) PC4buf (.D(adder_1_out), .en(1'b1), .clk(decoder_4_out1), .Q(PC4buf_q), .clr(button_1_out));
  Comparator #(.width(32)) comparator_1 (
    .a(multiplexer_1_out), .b(multiplexer_3_out), .eq(comparator_1_eq), .lt(comparator_1_lt));  // open: gt
  Comparator #(.mode("unsigned"), .width(32)) comparator_2 (
    .a(multiplexer_1_out), .b(multiplexer_3_out), .eq(comparator_2_eq), .lt(comparator_2_lt));  // open: gt
  Multiplexer #(.width(32)) multiplexer_8 (
    .in0(PC_q), .in1(multiplexer_17_out), .out({multiplexer_8_out, multiplexer_8_out_2}), .sel(counter_1_q[1]));
  Decoder #(.enable("false"), .select(3)) decoder_2 (
    .out1(decoder_2_out1), .out2(decoder_2_out2), .out3(decoder_2_out3), .sel(ROM_3_data));  // open: out0, out4, out5, out6, out7
  Divider #(.width(32)) divider_3 (
    .a(divider_2_out), .b(32'ha), .out(divider_3_out), .rem(divider_3_rem));  // open: upper
  Bit_Extender #(.in_width(32), .out_width(4)) bit_extender_5 (.in(divider_2_rem), .out(bit_extender_5_out));
  Divider #(.width(32)) divider_4 (
    .a(divider_3_out), .b(32'ha), .out(divider_4_out), .rem(divider_4_rem));  // open: upper
  Bit_Extender #(.in_width(32), .out_width(4)) bit_extender_6 (.in(divider_3_rem), .out(bit_extender_6_out));
  Multiplexer #(.width(32)) multiplexer_9 (
    .in0(adder_1_out), .in1(multiplexer_17_out), .out(multiplexer_9_out), .sel(multiplexer_10_out));
  Multiplexer multiplexer_10 (
    .in0(ROM_1_data[5]), .in1(multiplexer_13_out), .out(multiplexer_10_out), .sel(decoder_5_out3));
  not not_1 (not_1_out, comparator_1_eq);
  Multiplexer #(.select(2)) multiplexer_11 (
    .in0(comparator_1_eq), .in1(not_1_out), .in2(comparator_1_lt), .in3(not_2_out), .out(multiplexer_11_out),
    .sel(CIR_q_4));
  not not_2 (not_2_out, comparator_1_lt);
  not not_3 (not_3_out, comparator_2_eq);
  Multiplexer #(.select(2)) multiplexer_12 (
    .in0(comparator_2_eq), .in1(not_3_out), .in2(comparator_2_lt), .in3(not_4_out), .out(multiplexer_12_out),
    .sel(CIR_q_4));
  not not_4 (not_4_out, comparator_2_lt);
  Divider #(.width(32)) divider_5 (
    .a(divider_4_out), .b(32'ha), .out(divider_5_out), .rem(divider_5_rem));  // open: upper
  Bit_Extender #(.in_width(32), .out_width(4)) bit_extender_7 (.in(divider_4_rem), .out(bit_extender_7_out));
  Divider #(.width(32)) divider_6 (
    .a(divider_5_out), .b(32'ha), .out(divider_6_out), .rem(divider_6_rem));  // open: upper
  Bit_Extender #(.in_width(32), .out_width(4)) bit_extender_8 (.in(divider_5_rem), .out(bit_extender_8_out));
  Multiplexer multiplexer_13 (
    .in0(multiplexer_11_out), .in1(multiplexer_12_out), .out(multiplexer_13_out), .sel(CIR_q_5[3]));
  ROM #(.addrWidth(4), .dataWidth(7)) ROM_2 (
    .addr({CIR_q_5[3], CIR_q_4[0], multiplexer_8_out_2[1:0]}),
    .data({ROM_2_data[6], ROM_2_data_2, ROM_2_data[3:0]}));
  RAM #(.addrWidth(24), .asyncread("true"), .byteenables("byteEnables"), .dataWidth(32)) RAM_1 (
    .addr(multiplexer_8_out_2[25:2]), .we(decoder_2_out1), .oe(1'b1), .clk(and_1_out), .din(shifter_1_out),
    .dout(RAM_1_dout), .be3(ROM_2_data[3]), .be2(ROM_2_data[2]), .be1(ROM_2_data[1]), .be0(ROM_2_data[0]));
  Divider #(.width(32)) divider_7 (
    .a(divider_6_out), .b(32'ha), .out(divider_7_out), .rem(divider_7_rem));  // open: upper
  Bit_Extender #(.in_width(32), .out_width(4)) bit_extender_9 (.in(divider_6_rem), .out(bit_extender_9_out));
  Divider #(.width(32)) divider_8 (
    .a(divider_7_out), .b(32'ha), .out(divider_8_out), .rem(divider_8_rem));  // open: upper
  Bit_Extender #(.in_width(32), .out_width(4)) bit_extender_10 (.in(divider_7_rem), .out(bit_extender_10_out));
  Multiplexer #(.width(5)) multiplexer_14 (
    .in0(CIR_q_2), .in1({5{1'b0}}), .out(multiplexer_14_out), .sel(decoder_3_out0));
  Decoder #(.enable("false"), .select(2)) decoder_3 (
    .out0(decoder_3_out0), .out2(decoder_3_out2), .sel(ROM_1_data[4:3]));  // open: out1, out3
  Divider #(.width(32)) divider_9 (
    .a(divider_8_out), .b(32'ha), .out(divider_9_out), .rem(divider_9_rem));  // open: upper
  Bit_Extender #(.in_width(32), .out_width(4)) bit_extender_11 (.in(divider_8_rem), .out(bit_extender_11_out));
  Divider #(.width(32)) divider_10 (.a(divider_9_out), .b(32'ha), .rem(divider_10_rem));  // open: out, upper
  Bit_Extender #(.in_width(32), .out_width(4)) bit_extender_12 (.in(divider_9_rem), .out(bit_extender_12_out));
  Hex_Digit_Display #(.decimalPoint("false")) Hex_Digit_Display_9 (.value(bit_extender_13_out));
  Bit_Extender #(.in_width(32), .out_width(4)) bit_extender_13 (.in(divider_10_rem), .out(bit_extender_13_out));
  Adder #(.width(32)) adder_2 (
    .a(multiplexer_6_out), .b(multiplexer_7_out), .out(adder_2_out), .cin(1'b0));  // open: cout
  Subtractor #(.width(32)) subtractor_1 (
    .a(multiplexer_6_out), .b(multiplexer_7_out), .out(subtractor_1_out), .bin(1'b0));  // open: bout
  Shifter #(.width(32)) shifter_2 (.in(multiplexer_6_out), .\dist (multiplexer_7_out[4:0]), .out(shifter_2_out));
  Comparator #(.width(32)) comparator_3 (
    .a(multiplexer_6_out), .b(multiplexer_7_out), .lt(comparator_3_lt));  // open: gt, eq
  Comparator #(.mode("unsigned"), .width(32)) comparator_4 (
    .a(multiplexer_6_out), .b(multiplexer_7_out), .lt(comparator_4_lt));  // open: gt, eq
  assign xor_1_out = multiplexer_6_out ^ multiplexer_7_out;  // XOR_Gate xor_1, 32 bits wide
  Shifter #(.shift("lr"), .width(32)) shifter_3 (
    .in(multiplexer_6_out), .\dist (multiplexer_7_out[4:0]), .out(shifter_3_out));
  Shifter #(.shift("ar"), .width(32)) shifter_4 (
    .in(multiplexer_6_out), .\dist (multiplexer_7_out[4:0]), .out(shifter_4_out));
  assign or_1_out = multiplexer_6_out | multiplexer_7_out;  // OR_Gate or_1, 32 bits wide
  assign and_2_out = multiplexer_6_out & multiplexer_7_out;  // AND_Gate and_2, 32 bits wide
  Hex_Digit_Display #(.decimalPoint("false")) Hex_Digit_Display_1 (.value(x18_s2_q_8));
  Hex_Digit_Display #(.decimalPoint("false")) Hex_Digit_Display_10 (.value(bit_extender_12_out));
  Hex_Digit_Display #(.decimalPoint("false")) Hex_Digit_Display_11 (.value(bit_extender_11_out));
  Multiplexer #(.width(32)) multiplexer_15 (
    .in0(adder_2_out), .in1(subtractor_1_out), .out(multiplexer_15_out), .sel(and_3_out));
  assign bit_extender_14_out = {{31{1'b0}}, comparator_3_lt};  // Bit_Extender bit_extender_14
  assign bit_extender_15_out = {{31{1'b0}}, comparator_4_lt};  // Bit_Extender bit_extender_15
  Multiplexer #(.width(32)) multiplexer_16 (
    .in0(shifter_3_out), .in1(shifter_4_out), .out(multiplexer_16_out), .sel(and_3_out));
  Hex_Digit_Display #(.decimalPoint("false")) Hex_Digit_Display_2 (.value(x18_s2_q_7));
  Hex_Digit_Display #(.decimalPoint("false")) Hex_Digit_Display_3 (.value(x18_s2_q_6));
  Hex_Digit_Display #(.decimalPoint("false")) Hex_Digit_Display_12 (.value(bit_extender_10_out));
  Hex_Digit_Display #(.decimalPoint("false")) Hex_Digit_Display_13 (.value(bit_extender_9_out));
  Multiplexer #(.select(3), .width(32)) multiplexer_17 (
    .in0(multiplexer_15_out), .in1(shifter_2_out), .in2(bit_extender_14_out), .in3(bit_extender_15_out),
    .in4(xor_1_out), .in5(multiplexer_16_out), .in6(or_1_out), .in7(and_2_out), .out(multiplexer_17_out),
    .sel(multiplexer_22_out));
  Shifter #(.shift("lr"), .width(32)) shifter_5 (.in(RAM_1_dout), .\dist ({ROM_2_data_2, 3'b000}), .out(shifter_5_out));
  Hex_Digit_Display #(.decimalPoint("false")) Hex_Digit_Display_4 (.value(x18_s2_q_5));
  Hex_Digit_Display #(.decimalPoint("false")) Hex_Digit_Display_5 (.value(x18_s2_q_4));
  Hex_Digit_Display #(.decimalPoint("false")) Hex_Digit_Display_14 (.value(bit_extender_8_out));
  Hex_Digit_Display #(.decimalPoint("false")) Hex_Digit_Display_15 (.value(bit_extender_7_out));
  Register #(.width(32)) CIR (
    .D(RAM_1_dout), .en(1'b1), .clk(decoder_4_out1),
    .Q({CIR_q[31:25], CIR_q_3, CIR_q_6, CIR_q_4[1], CIR_q_5[3], CIR_q_4[0], CIR_q_2, CIR_q[6:0]}),
    .clr(button_1_out));
  Multiplexer #(.select(3), .width(32)) multiplexer_18 (
    .in0({32{1'b0}}), .in1(shifter_5_out), .in2({32{1'b0}}), .in3(multiplexer_5_out), .in4({32{1'b0}}),
    .in5({32{1'b0}}), .in6({32{1'b0}}), .in7({32{1'b0}}), .out(multiplexer_18_out), .sel(ROM_3_data));
  Hex_Digit_Display #(.decimalPoint("false")) Hex_Digit_Display_6 (.value(x18_s2_q_3));
  Hex_Digit_Display #(.decimalPoint("false")) Hex_Digit_Display_7 (.value(x18_s2_q_2));
  Hex_Digit_Display #(.decimalPoint("false")) Hex_Digit_Display_16 (.value(bit_extender_6_out));
  Hex_Digit_Display #(.decimalPoint("false")) Hex_Digit_Display_17 (.value(bit_extender_5_out));
  Bit_Extender #(.in_width(32), .\type ("zero")) bit_extender_16 (.in(multiplexer_18_out), .out(bit_extender_16_out));
  assign bit_extender_17_out = {{16{1'b0}}, bit_extender_16_out};  // Bit_Extender bit_extender_17
  assign bit_extender_18_out = {{16{bit_extender_16_out[15]}}, bit_extender_16_out};  // Bit_Extender bit_extender_18
  Bit_Extender #(.in_width(32), .out_width(8), .\type ("zero")) bit_extender_19 (
    .in(multiplexer_18_out), .out(bit_extender_19_out));
  assign bit_extender_20_out = {{24{1'b0}}, bit_extender_19_out};  // Bit_Extender bit_extender_20
  assign bit_extender_21_out = {{24{bit_extender_19_out[7]}}, bit_extender_19_out};  // Bit_Extender bit_extender_21
  Hex_Digit_Display #(.decimalPoint("false")) Hex_Digit_Display_8 (.value(x18_s2_q));
  Button button_1 (.out(button_1_out));
  Hex_Digit_Display #(.decimalPoint("false")) Hex_Digit_Display_18 (.value(bit_extender_4_out));
  Multiplexer #(.select(3), .width(32)) multiplexer_19 (
    .in0(bit_extender_21_out), .in1(bit_extender_18_out), .in2(multiplexer_18_out),
    .in4(bit_extender_20_out), .in5(bit_extender_17_out), .out(multiplexer_19_out),
    .sel({CIR_q_4[1], CIR_q_5[3], CIR_q_4[0]}));  // open: in3, in6, in7
  Multiplexer multiplexer_20 (.in0(clock_1_out), .in1(button_2_out), .out(multiplexer_20_out), .sel(dipswitch_1_sw1));
  Clock clock_1 (.out(clock_1_out));
  Button button_2 (.out(button_2_out));
  Counter #(.max('h3), .width(2)) counter_1 (
    .clr(button_1_out), .load(1'b0), .up(1'b1), .clk(multiplexer_20_out), .Q(counter_1_q));  // open: count, D, carry
  DipSwitch #(.number(2)) dipswitch_1 (.sw1(dipswitch_1_sw1));  // open: sw2
  and and_3 (and_3_out, CIR_q[30], multiplexer_21_out);
  Multiplexer #(.select(3)) multiplexer_21 (
    .in0(1'b1), .in1(nor_1_out), .in2(1'b0), .in3(1'b0), .in4(1'b0), .in5(1'b0), .out(multiplexer_21_out),
    .sel(ROM_1_data[2:0]));  // open: in6, in7
  not not_5 (not_5_out, multiplexer_22_out[0]);
  nor nor_1 (nor_1_out, not_5_out, not_6_out);
  not not_6 (not_6_out, multiplexer_22_out[2]);
  or or_2 (or_2_out, decoder_3_out2, decoder_5_out2, decoder_5_out3, or_3_out);
  ROM #(.addrWidth(7)) ROM_1 (.addr(CIR_q[6:0]), .data(ROM_1_data));
  Decoder #(.enable("false"), .select(2)) decoder_4 (
    .out0(decoder_4_out0), .out1(decoder_4_out1), .out3(decoder_4_out3), .sel(counter_1_q));  // open: out2
  Multiplexer #(.width(3)) multiplexer_22 (
    .in0({CIR_q_4[1], CIR_q_5[3], CIR_q_4[0]}), .in1(3'b000), .out(multiplexer_22_out), .sel(or_2_out));
  assign bit_extender_22_out = {{20{CIR_q[31]}}, {CIR_q[31:25], CIR_q_3}};  // Bit_Extender bit_extender_22
  assign bit_extender_23_out = {{20{CIR_q[31]}}, {CIR_q[31:25], CIR_q_2}};  // Bit_Extender bit_extender_23
  assign bit_extender_24_out = {{19{CIR_q[31]}}, {CIR_q[31], CIR_q_2[0], CIR_q[30:25], CIR_q_2[4:1], 1'b0}};  // Bit_Extender bit_extender_24
  assign bit_extender_25_out = {{11{CIR_q[31]}}, {CIR_q[31], CIR_q_6, CIR_q_4[1], CIR_q_5[3], CIR_q_4[0], CIR_q_3[0], CIR_q[30:25], CIR_q_3[4:1], 1'b0}};  // Bit_Extender bit_extender_25
  or or_3 (or_3_out, decoder_5_out4, decoder_5_out5);
  Decoder #(.enable("false"), .select(3)) decoder_5 (
    .out2(decoder_5_out2), .out3(decoder_5_out3), .out4(decoder_5_out4), .out5(decoder_5_out5),
    .sel(ROM_1_data[2:0]));  // open: out0, out1, out6, out7
  Multiplexer #(.select(3), .width(32)) multiplexer_23 (
    .in0({32{1'b0}}), .in1(bit_extender_22_out), .in2(bit_extender_23_out), .in3(bit_extender_24_out),
    .in4({CIR_q[31:25], CIR_q_3, CIR_q_6, CIR_q_4[1], CIR_q_5[3], CIR_q_4[0], {12{1'b0}}}),
    .in5(bit_extender_25_out), .in6({32{1'b0}}), .in7({32{1'b0}}), .out(multiplexer_23_out),
    .sel(ROM_1_data[2:0]));

  // Notes on the sheet:
  //   contents of ROM_3 (hex, n*v repeats v):
  //   1 31*0 2 15*0 3
  //   contents of ROM_2 (hex, n*v repeats v):
  //   1 12 24 38 3 40 2c 40 f 40 40 40
  //   contents of ROM_1 (hex, n*v repeats v):
  //   0 0 0 11 15*0 19 0 0 0 5c 11*0 2 15*0 98 0 0 0 1c 43*0 63 0 0 0 29 7*0 6d
endmodule
